// Logisim project alu.circ as structural Verilog
module main (
  input  [31:0] X,
  input  [31:0] Y,
  input  [5:0] Switch__S,
  output Signed_Overflow,
  output [31:0] RESULT,
  output Equal
);

  wire [31:0] and_out, or_out, sll_out;

  sll sll_1 (.inp1(X), .inp2(Y), .out(sll_out));
  srl srl_1 (.inp1(X), .inp2(Y), .out(sll_out));
  sra sra_1 (.inp1(X), .inp2(Y), .out(sll_out));
  assign and_out = X & Y;  // AND_Gate and, 32 bits wide
  assign or_out = X | Y;  // OR_Gate or, 32 bits wide
  Adder #(.width(32)) adder_1 (.a(X), .b(Y));  // open: out, cin, cout

  // Notes on the sheet:
  //   INPUTS to your circuit
  //   INPUT to your circuit
  //   DON'T CHANGE THE INPUTS AND OUTPUTS! IF YOU DO SO, YOU NEED TO MAKE SURE THE PINS ARE IN THE RIGHT PLACES!
  //   OUTPUTS of your circuit
endmodule

module sll (
  input  [31:0] inp1,
  input  [31:0] inp2,
  output [31:0] out
);

  wire [4:0] bit_extender_1_out;

  Bit_Extender #(.in_width(32), .out_width(5)) bit_extender_1 (.in(inp2), .out(bit_extender_1_out));
  Shifter #(.width(32)) shifter_1 (.in(inp1), .\dist (bit_extender_1_out), .out(out));
endmodule

module srl (
  input  [31:0] inp1,
  input  [31:0] inp2,
  output [31:0] out
);

  wire [4:0] bit_extender_1_out;

  Bit_Extender #(.in_width(32), .out_width(5)) bit_extender_1 (.in(inp2), .out(bit_extender_1_out));
  Shifter #(.width(32), .shift("lr")) shifter_1 (.in(inp1), .\dist (bit_extender_1_out), .out(out));
endmodule

module sra (
  input  [31:0] inp1,
  input  [31:0] inp2,
  output [31:0] out
);

  wire [4:0] bit_extender_1_out;

  Bit_Extender #(.in_width(32), .out_width(5)) bit_extender_1 (.in(inp2), .out(bit_extender_1_out));
  Shifter #(.width(32), .shift("ar")) shifter_1 (.in(inp1), .\dist (bit_extender_1_out), .out(out));
endmodule

module add (
  input  [31:0] inp1,
  input  [31:0] inp2,
  output [31:0] out,
  output overflow
);

  Adder #(.width(32)) adder_1 (.a(inp1), .b(inp2), .out(out), .cout(overflow));  // open: cin
endmodule

module addu (
  input  [31:0] inp1,
  input  [31:0] inp2,
  output [31:0] out
);

  Adder #(.width(32)) adder_1 (.a(inp1), .b(inp2), .out(out));  // open: cin, cout
endmodule

module sub (
  input  [31:0] inp1,
  input  [31:0] inp2,
  output [31:0] out,
  output overflow
);

  Subtractor #(.width(32)) subtractor_1 (.a(inp1), .b(inp2), .out(out), .bout(overflow));  // open: bin
endmodule

module subu (
  input  [31:0] inp1,
  input  [31:0] inp2,
  output [31:0] out
);

  Subtractor #(.width(32)) subtractor_1 (.a(inp1), .b(inp2), .out(out));  // open: bin, bout
endmodule

module slt (
  input  [31:0] inp1,
  input  [31:0] inp2,
  output [31:0] out
);

  wire comparator_1_lt;

  Comparator #(.width(32)) comparator_1 (.a(inp1), .b(inp2), .lt(comparator_1_lt));  // open: gt, eq
  assign out = {{31{1'b0}}, comparator_1_lt};  // Bit_Extender bit_extender_1
endmodule

module sltu (
  input  [31:0] inp1,
  input  [31:0] inp2,
  output [31:0] out
);

  wire comparator_1_lt;

  Comparator #(.width(32), .mode("unsigned")) comparator_1 (.a(inp1), .b(inp2), .lt(comparator_1_lt));  // open: gt, eq
  assign out = {{31{1'b0}}, comparator_1_lt};  // Bit_Extender bit_extender_1
endmodule
