// Logisim project cpu.circ as structural Verilog: 5 circuits, main circuit main
module main (
  input  [31:0] RS_READ_VALUE,
  input  [31:0] RT_READ_VALUE,
  input  [31:0] INSTRUCTION,
  input  CLOCK,
  input  RESET,
  output [31:0] t0,
  output [31:0] t1,
  output [31:0] t2,
  output [31:0] t3,
  output [4:0] RS,
  output [4:0] RT,
  output [4:0] Write_Register,
  output [31:0] RD_WRITE_VALUE,
  output RD_WRITE_ENABLE,
  output [23:0] FETCH_ADDRESS
);

  wire ALUSrc, Branch, check_if_t0_t3_1_if_t0_t3, check_if_t0_t3_2_if_t0_t3, check_if_t0_t3_3_if_t0_t3,
       MemToReg, opALU0, opALU1, ReadMem, RegDst, write_regfile, WriteMem, WriteReg;
  wire [31:0] multiplexer_2_out, multiplexer_3_out, regfile_wrapper_read_data_1, regfile_wrapper_read_data_2;

  not not_1 (RD_WRITE_ENABLE, write_regfile);
  Multiplexer #(.width(5)) multiplexer_1 (
    .in0(INSTRUCTION[20:16]), .in1(INSTRUCTION[15:11]), .out(Write_Register), .sel(RegDst));  // open: en
  check_if_t0_t3 check_if_t0_t3_1 (.\reg (Write_Register), .if_t0_t3(check_if_t0_t3_1_if_t0_t3));
  cpu_control cpu_control_1 (
    .opcode(INSTRUCTION[31:26]), .RegDest(RegDst), .ALUSrc(ALUSrc), .MemToReg(MemToReg), .WriteReg(WriteReg),
    .ReadMem(ReadMem), .WriteMem(WriteMem), .Branch(Branch), .opALU1(opALU1), .opALU0(opALU0));
  and and_1 (write_regfile, check_if_t0_t3_1_if_t0_t3, WriteReg);
  regfile_wrapper regfile_wrapper (
    .read_register_1(INSTRUCTION[25:21]), .read_register_2(INSTRUCTION[20:16]),
    .write_register(Write_Register), .RegWrite(write_regfile), .clock(CLOCK),
    .read_data_1(regfile_wrapper_read_data_1), .read_data_2(regfile_wrapper_read_data_2));  // open: write_data
  check_if_t0_t3 check_if_t0_t3_2 (.\reg (INSTRUCTION[25:21]), .if_t0_t3(check_if_t0_t3_2_if_t0_t3));
  check_if_t0_t3 check_if_t0_t3_3 (.\reg (INSTRUCTION[20:16]), .if_t0_t3(check_if_t0_t3_3_if_t0_t3));
  // alu_main ALU: pin names not known
  // regfile_main RegFile: pin names not known
  Multiplexer #(.width(32)) multiplexer_2 (
    .in0(RS_READ_VALUE), .in1(regfile_wrapper_read_data_1), .out(multiplexer_2_out),
    .sel(check_if_t0_t3_2_if_t0_t3));  // open: en
  Multiplexer #(.width(32)) multiplexer_3 (
    .in0(RT_READ_VALUE), .in1(regfile_wrapper_read_data_2), .out(multiplexer_3_out),
    .sel(check_if_t0_t3_3_if_t0_t3));  // open: en
  // mem_main MEM: pin names not known

  assign RS = INSTRUCTION[25:21];
  assign RT = INSTRUCTION[20:16];

  // Other names for the same wires on the sheet: clk = CLOCK; rd[4:0] = INSTRUCTION[15:11];
  //   opcode[5:0] = INSTRUCTION[31:26]; rt_rd[4:0] = Write_Register; run_rs_val[31:0] = RS_READ_VALUE;
  //   run_rt_val[31:0] = RT_READ_VALUE

  // Notes on the sheet:
  //   These are outputs/inputs from run.circ
  //   These are outputs to run.circ
  //   Feel free to move these components
endmodule

module check_if_t0_t3 (
  input  [4:0] \reg ,
  output if_t0_t3
);

  wire comparator_1_lt, comparator_2_gt;

  Comparator #(.width(5), .mode("unsigned")) comparator_1 (
    .a(\reg ), .b(5'b01100), .lt(comparator_1_lt));  // open: gt, eq
  Comparator #(.width(5), .mode("unsigned")) comparator_2 (
    .a(\reg ), .b(5'b00111), .gt(comparator_2_gt));  // open: eq, lt
  and \and  (if_t0_t3, comparator_1_lt, comparator_2_gt);
endmodule

module rs_rt_val (
  input  [31:0] run_rs_val,
  input  [4:0] rs,
  input  [4:0] rt,
  input  [31:0] run_rt_val,
  output [31:0] rs_val,
  output [31:0] rt_val
);

  wire check_if_rs_t0_t3_2_if_t0_t3, check_if_rs_t0_t3_if_t0_t3;
  wire [1:0] bit_extender_1_out, bit_extender_2_out;
  wire [31:0] regfile_read_data_1, regfile_read_data_2;

  check_if_t0_t3 check_if_rs_t0_t3 (.\reg (rs), .if_t0_t3(check_if_rs_t0_t3_if_t0_t3));
  Bit_Extender #(.in_width(5), .out_width(2)) bit_extender_1 (.in(rs), .out(bit_extender_1_out));
  Bit_Extender #(.in_width(5), .out_width(2)) bit_extender_2 (.in(rt), .out(bit_extender_2_out));
  check_if_t0_t3 check_if_rs_t0_t3_2 (.\reg (rt), .if_t0_t3(check_if_rs_t0_t3_2_if_t0_t3));
  regfile_main regfile (
    .Read_register_1(bit_extender_1_out), .Read_register_2(bit_extender_2_out),
    .Read_Data_1(regfile_read_data_1), .Read_Data_2(regfile_read_data_2));  // open: write_register, write_data, t0_Value, t1_Value, t2_Value, t3_Value, RegWrite, clock
  Multiplexer #(.width(32)) multiplexer_1 (
    .in0(run_rs_val), .in1(regfile_read_data_1), .out(rs_val), .sel(check_if_rs_t0_t3_if_t0_t3));  // open: en
  Multiplexer #(.width(32)) multiplexer_2 (
    .in0(run_rt_val), .in1(regfile_read_data_2), .out(rt_val), .sel(check_if_rs_t0_t3_2_if_t0_t3));  // open: en
endmodule

module cpu_control (
  input  [5:0] opcode,
  output RegDest,
  output ALUSrc,
  output MemToReg,
  output WriteReg,
  output ReadMem,
  output WriteMem,
  output Branch,
  output opALU1,
  output opALU0
);

  wire not_1_out, not_2_out, not_3_out, not_4_out, not_5_out, not_6_out, not_7_out, not_8_out, not_9_out,
       not_10_out, not_11_out, not_12_out, not_13_out, not_14_out, not_15_out, not_16_out;

  not not_1 (not_1_out, opcode[5]);
  not not_2 (not_2_out, opcode[3]);
  not not_3 (not_3_out, opcode[1]);
  not not_4 (not_4_out, opcode[0]);
  not not_5 (not_5_out, opcode[4]);
  not not_6 (not_6_out, opcode[2]);
  and and_1 (opALU1, not_1_out, not_5_out, not_2_out, not_6_out, not_3_out, not_4_out);
  not not_7 (not_7_out, opcode[2]);
  not not_8 (not_8_out, opcode[4]);
  not not_9 (not_9_out, opcode[3]);
  and and_2 (MemToReg, opcode[5], not_8_out, not_9_out, not_7_out, opcode[1], opcode[0]);
  not not_10 (not_10_out, opcode[4]);
  and and_3 (WriteMem, opcode[5], not_10_out, opcode[3], not_11_out, opcode[1], opcode[0]);
  not not_11 (not_11_out, opcode[2]);
  not not_12 (not_12_out, opcode[4]);
  not not_13 (not_13_out, opcode[5]);
  not not_14 (not_14_out, opcode[3]);
  not not_15 (not_15_out, opcode[1]);
  not not_16 (not_16_out, opcode[0]);
  and and_4 (Branch, not_13_out, not_12_out, not_14_out, opcode[2], not_15_out, not_16_out);
  or or_1 (ALUSrc, MemToReg, WriteMem);
  or or_2 (WriteReg, opALU1, MemToReg);

  assign opALU0 = Branch;
  assign ReadMem = MemToReg;
  assign RegDest = opALU1;
endmodule

module regfile_wrapper (
  input  [4:0] read_register_1,
  input  [4:0] read_register_2,
  input  [4:0] write_register,
  input  RegWrite,
  input  clock,
  input  [31:0] write_data,
  output [31:0] read_data_1,
  output [31:0] read_data_2
);

  wire [1:0] bit_extender_1_out, bit_extender_2_out, bit_extender_3_out;

  Bit_Extender #(.in_width(5), .out_width(2)) bit_extender_1 (.in(read_register_1), .out(bit_extender_1_out));
  Bit_Extender #(.in_width(5), .out_width(2)) bit_extender_2 (.in(read_register_2), .out(bit_extender_2_out));
  Bit_Extender #(.in_width(5), .out_width(2)) bit_extender_3 (.in(write_register), .out(bit_extender_3_out));
  regfile_main regfile (
    .Read_register_1(bit_extender_1_out), .Read_register_2(bit_extender_2_out),
    .write_register(bit_extender_3_out), .write_data(write_data), .RegWrite(RegWrite), .clock(clock),
    .Read_Data_1(read_data_1), .Read_Data_2(read_data_2));  // open: t0_Value, t1_Value, t2_Value, t3_Value

  // Notes on the sheet:
  //   regfile wrapper whose register inputs are 5 bits rather than 2 bits
endmodule
